# Fritzing sketch Gaz_detection (saved by Fritzing 0.9.3b)
breadboards: 1

parts:
  U1 = ESP32-38PinWide [part_number=ESP32-38PinWide]
  Composant3 = MQ-3 breakout
  LED1 = smd LED [color="Red (633nm)" package="0603 [SMD]"]
  LED2 = smd LED [color="Green (555nm)" package="0603 [SMD]"]
  J1 = Piezo Speaker
  R1 = Resistor [tolerance=±5% resistance=220 package="1206 [SMD]"]
  R2 = Resistor [tolerance=±5% resistance=220 package="2010 [SMD]"]
  USBTTL1 = Micro USB B Plug  # not connected

nets:
  N1: U1.3.3, Composant3.VCC
  N2: U1.GPIO34, Composant3.AO
  N3: U1.GPIO25, J1.pin2
  N4: U1.GPIO26, R1.Pin_1
  N5: U1.GPIO27, R2.Pin_1
  N6: Composant3.GND, LED1.cathode, LED2.cathode, J1.pin1
  N7: LED1.anode, R2.Pin_0
  N8: LED2.anode, R1.Pin_0

custom parts:
  ESP32-38PinWide: Generic 38-Pin ESP32 with wide format (only access to one side of pins on a breadboard) based on Stephen Lilley's HiLetgo ESP-WROOM-32 ESP32 ESP-32S Development Board.
  MQ-3 breakout: Alcohol sensor is capable of detecting alcohol (ethanol) particles on itself and gives the information in digital form back to us to manipulate with it. SKU:101251 • Voltage: 5V DC • Power: max 750mW • Measurement range: 0.04-4mg/L
